# Fritzing sketch Layout (saved by Fritzing 0.9.3b)
breadboards: 1

parts:
  U1 = TEMPERATURE-SENSOR [package=to-92]
  U2 = NodeMCU V1.0
  LED1 = RGB LED - (4 legs) [package="5 mm [THT]"]
  R2 = Resistor [tolerance=±5% resistance=470 package="1206 [SMD]"]

nets:
  N1: U1.GND, U2.D3, R2.Pin_1
  N2: U1.ADJ, U2.GND, LED1.common_anode
  N3: U1.VCC, R2.Pin_0
  N4: U2.D4, LED1.red_cathode
  N5: U2.D5, LED1.green_cathode
  N6: U2.D6, LED1.blue_cathode

custom parts:
  NodeMCU V1.0: ESP8266 based NodeMCU
